# Fritzing sketch neopixelmask-wiring (saved by Fritzing 0.9.2b)

parts:
  Part1 = Photon
  S1 = Round Pushbutton
  U1 = SWITCH_SPDT [package=kps-1290]
  NEOPIXEL2 = Neopixel Strip -- Black (30/m)

nets:
  N1: Part1.A5, NEOPIXEL2.+5V
  GND: Part1.GND, NEOPIXEL2.GND
  N2: Part1.VIN, NEOPIXEL2.DI
  N3: Part1.D1, U1.P
  N4: Part1.D2, S1.leg0
  N5: Part1.VBAT, S1.leg1
  N6: Part1.3V3, U1.S

custom parts:
  Neopixel Strip -- Black (30/m): Neopixel Strip, Black, 30 pixels per meter.
